# Fritzing sketch Sophy Schematics (saved by Fritzing 0.9.3b)
circuit board: 2.07076cm x 2.21089cm
breadboards: 1

parts:
  Raspberry_Pi_1 = Raspberry Pi 3 [part_number=RPI-3-V1.2]
  R1 = Resistor [tolerance=±5% resistance=56 package=THT]
  IC1 = DIP - 4 pins [chip_label=ELI package="DIP (Dual Inline) [THT]"]
  R2 = Resistor [tolerance=±5% resistance=1.5k package=THT]
  R3 = Resistor [tolerance=±5% resistance=10k package=THT]
  Q2 = NPN-Transistor [package="TO92 [THT]"]
  R4 = Resistor [tolerance=±5% resistance=10k package=THT]
  R5 = Resistor [tolerance=±5% resistance=3.3k package=THT]
  J1 = male pin header, 4 pins [form="♂ (male)"]

nets:
  N1: Raspberry_Pi_1.3v3, R1.Pin_0, IC1.4, J1.pin2
  D1: Raspberry_Pi_1.GPIO4, Q2.E, R4.Pin_1, J1.pin3
  N2: Raspberry_Pi_1.GND, IC1.2, R2.Pin_1, R4.Pin_0, J1.pin4
  5V: Raspberry_Pi_1.5V, R5.Pin_0, J1.pin1
  N3: R1.Pin_1, IC1.1
  N4: IC1.3, R2.Pin_0, R3.Pin_0
  N5: R3.Pin_1, Q2.B
  N6: Q2.C, R5.Pin_1

notes:
  Q
  5V
  3V
  G

custom parts:
  DIP - 4 pins: A DIP stand-in part for whatever IC you want. With 4 pins on a 300mil dual inline package (DIP) footprint.
